# Fritzing sketch Circuit Diagram (saved by Fritzing 0.9.3b)

parts:
  Buzzer1 = Piezo Speaker [part_number="RS 535-8253"]
  Part1 = Adafruit HUZZAH32 ESP32 Feather [part_number="Adafruit #3405"]
  R4 = Resistor [tolerance=±5% resistance=180 package="1206 [SMD]"]
  Momentary_Switch1 = Momentary Switch [package=ksa_sealed_tac_switch]
  R2 = Resistor [tolerance=±5% resistance=12k package="1206 [SMD]"]
  R1 = Resistor [tolerance=±0.1% resistance=1M package="1206 [SMD]"]
  R7 = Resistor [tolerance=±1% resistance=220k package="1206 [SMD]"]
  R3 = Resistor [tolerance=±5% resistance=180 package="1206 [SMD]"]
  R5 = Resistor [tolerance=±5% resistance=180 package="1206 [SMD]"]
  5050_RGB_LED = IC, DIP package, 6 pins [chip_label="5050 RGB LED"]
  R6 = Resistor [tolerance=±0.1% resistance=1M package="1206 [SMD]"]

nets:
  N1: Buzzer1.pin1, Part1.A1_DAC1
  N2: Buzzer1.pin2, R6.Pin_1
  N3: Part1.A0_DAC2, R1.Pin_0, R7.Pin_0
  N4: Part1.GND, Momentary_Switch1.2, R7.Pin_1, 5050_RGB_LED.pin4, 5050_RGB_LED.pin5, 5050_RGB_LED.pin6, R6.Pin_0
  N5: Part1.3.3V, R2.Pin_1
  N6: Part1.VBAT, R1.Pin_1
  N7: Part1.IO13_A12, R5.Pin_1
  N8: Part1.IO12_A11, R4.Pin_1
  N9: Part1.IO27_A10, R3.Pin_1
  N10: Part1.IO32_A7, Momentary_Switch1.4
  N11: R4.Pin_0, 5050_RGB_LED.pin2
  N12: Momentary_Switch1.3, R2.Pin_0
  N13: R3.Pin_0, 5050_RGB_LED.pin3
  N14: R5.Pin_0, 5050_RGB_LED.pin1

notes:
  Maker Appliances: Pushy Featherwing
  MAB02
  All components are available on the pre-prepared Pushy Featherwing which can be connected to an Adafruit Feather Huzzah32 using the standard pins that come with the two boards.
  This schematic is shared under the GNU General Public License v3.0.
  www.m-appliances.com
  github.com/maker-appliances/Pushy
